# Fritzing sketch Schematics (saved by Fritzing 0.9.3b)
breadboards: 1

parts:
  Part1 = Arduino Uno (Rev3)
  M1 = Stepper Motor - Bipolar
  U1 = prefix0000
  Espessif_Serial_Wifi_Modul_1 = ESP8266 ESP01 [part_number=ESP8266 package=THT]
  R1 = Resistor [tolerance=±5% resistance=10k part_number=10kΩ package="0603 [SMD]"]
  R2 = Resistor [tolerance=±5% resistance=2k package=THT]
  R3 = Resistor [tolerance=±5% resistance=1k package="0603 [SMD]"]
  M2 = Stepper Motor - Bipolar
  U2 = prefix0000
  Power_plug1 = Power plug [part_number="24V DC"]

nets:
  N1: Part1.D10_PWM/SS, U1.connector11
  N2: Part1.D11_PWM/MOSI, U1.connector9
  N3: Part1.D12/MISO, U2.connector11
  N4: Part1.D13/SCK, U2.connector9
  GND: Part1.GND, U1.connector8, U1.connector10, Espessif_Serial_Wifi_Modul_1.GND, R2.Pin_0, U2.connector8, U2.connector10
  N5: Part1.D2, Espessif_Serial_Wifi_Modul_1.TXD
  N6: Part1.D3_PWM, R3.Pin_1
  3V3: Part1.3V3, Espessif_Serial_Wifi_Modul_1.VCC, R1.Pin_0
  N7: M1.A, U1.connector3
  N8: M1.C, U1.connector2
  N9: M1.B, U1.connector1
  N10: M1.D, U1.connector0
  N11: U1.connector4, U2.connector4, Power_plug1.VCC
  N12: U1.connector5, U2.connector5, Power_plug1.GND
  N13: Espessif_Serial_Wifi_Modul_1.RXD, R2.Pin_1, R3.Pin_0
  N14: Espessif_Serial_Wifi_Modul_1.CH_PD, R1.Pin_1
  N15: M2.A, U2.connector3
  N16: M2.C, U2.connector2
  N17: M2.B, U2.connector1
  N18: M2.D, U2.connector0

notes:
  10kΩ
  1kΩ
  2kΩ
  24v DC
  ESP 01

custom parts:
  ESP8266 ESP01: Generic WiFi Module based on the ESP8266 with onboard PCB antenna and UART communications
